# Fritzing sketch LED and switch on Pi (saved by Fritzing 0.9.6b)
breadboards: 1

parts:
  Raspberry_Pi1 = Raspberry Pi B+
  LED1 = LED - 5mm [color="Red (633nm)" current=0.030 package="5 mm [THT]"]
  R1 = Resistor [tolerance=±20% power=0.25 resistance=330 package=THT]
  S1 = Momentary Switch [package=tactile-pth]

nets:
  N1: Raspberry_Pi1.GPIO2, S1.1
  N2: Raspberry_Pi1.GPIO18, LED1.anode
  N3: Raspberry_Pi1.GND, R1.Pin_0, S1.2
  N4: LED1.cathode, R1.Pin_1
