# Fritzing sketch LED button and buzzer on Pi (saved by Fritzing 1.0.7)
breadboards: 1

parts:
  Raspberry_Pi1 = Raspberry Pi B+
  LED1 = LED - 5mm [color="Red (633nm)" current=0.030 package="5 mm [THT]"]
  R1 = Resistor [tolerance=±20% power=0.25 resistance=330 package=THT]
  S1 = Momentary Switch [package=tactile-pth]
  J1 = Piezo Speaker
  PIR1 = PIR sensor

nets:
  N1: Raspberry_Pi1.GPIO2, S1.1
  N2: Raspberry_Pi1.GPIO24, J1.pin2
  N3: Raspberry_Pi1.GPIO23, PIR1.SIG
  N4: Raspberry_Pi1.GPIO18, LED1.anode
  GND: Raspberry_Pi1.GND, R1.Pin_0, S1.2, J1.pin1, PIR1.GND
  5V: Raspberry_Pi1.5V, PIR1.VDD
  N5: LED1.cathode, R1.Pin_1
