# Fritzing sketch distance sensor on pi (saved by Fritzing 0.9.6b)
breadboards: 1

parts:
  Raspberry_Pi1 = Raspberry Pi B+
  HC-SR04_Sensor_1 = HC-SR04 Ultrasonic Distance Sensor
  R1 = Resistor [tolerance=±5% power=0.25 resistance=1k package=THT]
  R2 = Resistor [tolerance=±5% power=0.25 resistance=1k package=THT]
  R3 = Resistor [tolerance=±5% power=0.25 resistance=1k package=THT]

nets:
  N1: Raspberry_Pi1.GPIO4, HC-SR04_Sensor_1.TRIG
  N2: Raspberry_Pi1.GPIO17, R1.Pin_1, R2.Pin_0
  GND: Raspberry_Pi1.GND, HC-SR04_Sensor_1.GND, R3.Pin_1
  5V: Raspberry_Pi1.5V, HC-SR04_Sensor_1.VCC
  N3: HC-SR04_Sensor_1.ECHO, R1.Pin_0
  N4: R2.Pin_1, R3.Pin_0
