# Fritzing sketch stepper motor on Pi (saved by Fritzing 0.9.6b)
breadboards: 1

parts:
  Raspberry_Pi1 = Raspberry Pi B+
  LED1 = LED - 5mm [color="Red (633nm)" current=0.030 package="5 mm [THT]"]
  R1 = Resistor [tolerance=±20% power=0.25 resistance=330 package=THT]
  S1 = Momentary Switch [package=tactile-pth]
  SM1 = 28BYJ-48 Stepper Motor [part_number=28BYJ-48]
  Driver1 = 28BYJ-48 Driver Module [part_number=ULN2003 package=THT]

nets:
  N1: Raspberry_Pi1.GPIO2, S1.1
  N2: Raspberry_Pi1.GPIO21, Driver1.IN4
  N3: Raspberry_Pi1.GPIO20, Driver1.IN3
  N4: Raspberry_Pi1.GPIO16, Driver1.IN2
  N5: Raspberry_Pi1.GPIO12, Driver1.IN1
  N6: Raspberry_Pi1.GPIO18, LED1.anode
  GND: Raspberry_Pi1.GND, R1.Pin_0, S1.2, Driver1.GND
  N7: Raspberry_Pi1.5V, Driver1.Vmotor
  N8: LED1.cathode, R1.Pin_1
  N9: SM1.blue-pin, Driver1.blue-pin
  N10: SM1.pink-pin, Driver1.pink-pin
  N11: SM1.yellow-pin, Driver1.yellow-pin
  N12: SM1.orange-pin, Driver1.orange-pin
  N13: SM1.red-pin, Driver1.red-pin

custom parts:
  28BYJ-48 Stepper Motor: Unipolar Stepper Motor 28BYJ-48 Top coil - pink & orange Bottom coil - blue & yellow Common rail - red Connector pins: blue - pink - yellow - orange - red
  28BYJ-48 Driver Module: Generic male header
